// Logisim project lab2_7seg.circ as structural Verilog: 9 circuits, main circuit LogiHexChecker
module LogiHexChecker (
);

  wire hexdecoder_1_s0, hexdecoder_1_s1, hexdecoder_1_s2, hexdecoder_1_s3, hexdecoder_1_s4, hexdecoder_1_s5,
       hexdecoder_1_s6;
  wire [3:0] dipswitch_1_p1;

  // DipSwitch #(.number(4)) dipswitch_1: pin names not known; wires that end beside it: dipswitch_1_p1[0], dipswitch_1_p1[1], dipswitch_1_p1[2], dipswitch_1_p1[3]
  _7_Segment_Display #(.decimalPoint("false")) u_7_segment_display_1 (
    .g(hexdecoder_1_s6), .f(hexdecoder_1_s5), .a(hexdecoder_1_s0), .b(hexdecoder_1_s1), .e(hexdecoder_1_s4),
    .d(hexdecoder_1_s3), .c(hexdecoder_1_s2));
  Hex_Digit_Display #(.decimalPoint("false")) hex_digit_display_1 (.value(dipswitch_1_p1));
  HexDecoder hexdecoder_1 (
    .D0(dipswitch_1_p1[0]), .D1(dipswitch_1_p1[1]), .D2(dipswitch_1_p1[2]), .D3(dipswitch_1_p1[3]),
    .S0(hexdecoder_1_s0), .S1(hexdecoder_1_s1), .S2(hexdecoder_1_s2), .S3(hexdecoder_1_s3),
    .S4(hexdecoder_1_s4), .S5(hexdecoder_1_s5), .S6(hexdecoder_1_s6));
endmodule

module HexDecoder (
  input  D0,
  input  D1,
  input  D2,
  input  D3,
  output S0,
  output S1,
  output S2,
  output S3,
  output S4,
  output S5,
  output S6
);

  Hex0 hex0_1 (.D3(D3), .D2(D2), .D1(D1), .D0(D0), .S0(S0));
  Hex1 hex1_1 (.D3(D3), .D2(D2), .D1(D1), .D0(D0), .S1(S1));
  Hex2 hex2_1 (.D3(D3), .D2(D2), .D1(D1), .D0(D0), .S2(S2));
  Hex3 hex3_1 (.D3(D3), .D2(D2), .D1(D1), .D0(D0), .S3(S3));
  Hex4 hex4_1 (.D3(D3), .D2(D2), .D1(D1), .D0(D0), .S4(S4));
  Hex5 hex5_1 (.D3(D3), .D2(D2), .D1(D1), .D0(D0), .S5(S5));
  Hex6 hex6_1 (.D3(D3), .D2(D2), .D1(D1), .D0(D0), .S6(S6));
endmodule

module Hex0 (
  input  D3,
  input  D2,
  input  D1,
  input  D0,
  output S0
);

  wire and_1_out, and_2_out, and_3_out, and_4_out, and_5_out, not_1_out, not_2_out, not_3_out, not_4_out;

  not not_1 (not_1_out, D3);
  not not_2 (not_2_out, D2);
  not not_3 (not_3_out, D1);
  not not_4 (not_4_out, D0);
  and and_1 (and_1_out, not_2_out, not_4_out);
  and and_2 (and_2_out, not_1_out, D1);
  and and_3 (and_3_out, not_1_out, D2, D0);
  and and_4 (and_4_out, D3, not_2_out, not_3_out);
  and and_5 (and_5_out, D2, D1);
  or or_1 (S0, and_1_out, and_2_out, and_3_out, and_4_out, and_5_out);
endmodule

module Hex1 (
  input  D3,
  input  D2,
  input  D1,
  input  D0,
  output S1
);

  wire and_1_out, and_2_out, and_3_out, and_4_out, and_5_out, not_1_out, not_2_out, not_3_out, not_4_out;

  not not_1 (not_1_out, D3);
  not not_2 (not_2_out, D2);
  not not_3 (not_3_out, D1);
  not not_4 (not_4_out, D0);
  and and_1 (and_1_out, not_1_out, not_3_out, not_4_out);
  and and_2 (and_2_out, not_1_out, D1, D0);
  and and_3 (and_3_out, not_2_out, not_4_out);
  and and_4 (and_4_out, D3, not_3_out, D0);
  and and_5 (and_5_out, not_1_out, not_2_out);
  or or_1 (S1, and_1_out, and_2_out, and_3_out, and_4_out, and_5_out);
endmodule

module Hex2 (
  input  D3,
  input  D2,
  input  D1,
  input  D0,
  output S2
);

  wire and_1_out, and_2_out, and_3_out, and_4_out, and_5_out, not_1_out, not_2_out, not_3_out;

  not not_1 (not_1_out, D3);
  not not_2 (not_2_out, D2);
  not not_3 (not_3_out, D1);
  and and_1 (and_1_out, not_1_out, D2);
  and and_2 (and_2_out, D3, not_2_out);
  and and_3 (and_3_out, not_3_out, D0);
  and and_4 (and_4_out, not_1_out, not_3_out);
  and and_5 (and_5_out, not_1_out, D0);
  or or_1 (S2, and_1_out, and_2_out, and_3_out, and_4_out, and_5_out);
endmodule

module Hex3 (
  input  D3,
  input  D2,
  input  D1,
  input  D0,
  output S3
);

  wire and_1_out, and_2_out, and_3_out, and_4_out, and_5_out, and_6_out, and_7_out, and_8_out, not_1_out,
       not_2_out, not_3_out, not_4_out;

  not not_1 (not_1_out, D3);
  not not_2 (not_2_out, D2);
  not not_3 (not_3_out, D1);
  not not_4 (not_4_out, D0);
  and and_1 (and_1_out, D2, not_3_out, D0);
  and and_2 (and_2_out, not_1_out, not_2_out, not_4_out);
  and and_3 (and_3_out, not_1_out, not_2_out, D1);
  and and_4 (and_4_out, not_1_out, D1, not_4_out);
  and and_5 (and_5_out, not_2_out, not_3_out, not_4_out);
  and and_6 (and_6_out, D3, not_3_out);
  and and_7 (and_7_out, not_2_out, D1, D0);
  and and_8 (and_8_out, D2, D1, not_4_out);
  or or_1 (S3, and_1_out, and_2_out, and_3_out, and_4_out, and_5_out, and_6_out, and_7_out, and_8_out);
endmodule

module Hex4 (
  input  D3,
  input  D2,
  input  D1,
  input  D0,
  output S4
);

  wire and_1_out, and_2_out, and_3_out, and_4_out, not_1_out, not_2_out;

  not not_1 (not_1_out, D2);
  not not_2 (not_2_out, D0);
  and and_1 (and_1_out, not_1_out, not_2_out);
  and and_2 (and_2_out, D1, not_2_out);
  and and_3 (and_3_out, D3, D1);
  and and_4 (and_4_out, D3, D2);
  or or_1 (S4, and_1_out, and_2_out, and_3_out, and_4_out);
endmodule

module Hex5 (
  input  D3,
  input  D2,
  input  D1,
  input  D0,
  output S5
);

  wire and_1_out, and_2_out, and_3_out, and_4_out, and_5_out, not_1_out, not_2_out, not_3_out, not_4_out;

  not not_1 (not_1_out, D3);
  not not_2 (not_2_out, D2);
  not not_3 (not_3_out, D1);
  not not_4 (not_4_out, D0);
  and and_1 (and_1_out, not_1_out, D2, not_3_out);
  and and_2 (and_2_out, D3, not_2_out);
  and and_3 (and_3_out, D3, D1);
  and and_4 (and_4_out, not_1_out, not_3_out, not_4_out);
  and and_5 (and_5_out, not_1_out, D2, not_4_out);
  or or_1 (S5, and_1_out, and_2_out, and_3_out, and_4_out, and_5_out);
endmodule

module Hex6 (
  input  D3,
  input  D2,
  input  D1,
  input  D0,
  output S6
);

  wire and_1_out, and_2_out, and_3_out, not_1_out, not_2_out, not_3_out;

  not not_1 (not_1_out, D2);
  not not_2 (not_2_out, D1);
  not not_3 (not_3_out, D0);
  and and_1 (and_1_out, not_1_out, D1);
  and and_2 (and_2_out, D2, not_2_out);
  and and_3 (and_3_out, D1, not_3_out);
  or or_1 (S6, and_1_out, and_2_out, D3, and_3_out);
endmodule
