// Logisim project lab2_mux.circ as structural Verilog: 8 circuits, main circuit MuxChecker
module MuxChecker (
  input  [3:0] in_1,
  input  [1:0] in_2
);

  wire aoi22mux41_1_y, hierarchicalmux41_1_y, twolevelmux41_1_y;

  TwoLevelMux41 twolevelmux41_1 (
    .S0(in_2[0]), .S1(in_2[1]), .D0(in_1[0]), .D1(in_1[1]), .D2(in_1[2]), .D3(in_1[3]), .Y(twolevelmux41_1_y));
  HierarchicalMux41 hierarchicalmux41_1 (
    .S0(in_2[0]), .S1(in_2[1]), .D0(in_1[0]), .D1(in_1[1]), .D2(in_1[2]), .D3(in_1[3]),
    .Y(hierarchicalmux41_1_y));
  AOI22Mux41 aoi22mux41_1 (
    .S0(in_2[0]), .S1(in_2[1]), .D0(in_1[0]), .D1(in_1[1]), .D2(in_1[2]), .D3(in_1[3]), .Y(aoi22mux41_1_y));
  LED led_1 (.in(twolevelmux41_1_y));
  LED led_2 (.in(hierarchicalmux41_1_y));
  LED led_3 (.in(aoi22mux41_1_y));

  // Other names for the same wires on the sheet: D0 = in_1[0]; D1 = in_1[1]; D2 = in_1[2]; D3 = in_1[3]; S0 = in_2[0];
  //   S1 = in_2[1]
endmodule

module Mux21 (
  input  S,
  input  D0,
  input  D1,
  output Y
);

  wire and_1_out, and_2_out, not_1_out;

  not not_1 (not_1_out, S);
  and and_1 (and_1_out, D0, not_1_out);
  and and_2 (and_2_out, D1, S);
  or or_1 (Y, and_1_out, and_2_out);
endmodule

module TwoLevelMux41 (
  input  S0,
  input  S1,
  input  D0,
  input  D1,
  input  D2,
  input  D3,
  output Y
);

  wire and_1_out, and_2_out, and_3_out, and_4_out, not_1_out, not_2_out;

  not not_1 (not_1_out, S1);
  not not_2 (not_2_out, S0);
  and and_1 (and_1_out, not_1_out, not_2_out, D0);
  and and_2 (and_2_out, not_1_out, S0, D1);
  and and_3 (and_3_out, S1, not_2_out, D2);
  and and_4 (and_4_out, S1, S0, D3);
  or or_1 (Y, and_1_out, and_2_out, and_3_out, and_4_out);
endmodule

module HierarchicalMux41 (
  input  S0,
  input  S1,
  input  D0,
  input  D1,
  input  D2,
  input  D3,
  output Y
);

  wire mux21_1_y, mux21_2_y;

  Mux21 mux21_1 (.S(S0), .D0(D0), .D1(D1), .Y(mux21_1_y));
  Mux21 mux21_2 (.S(S0), .D0(D2), .D1(D3), .Y(mux21_2_y));
  Mux21 mux21_3 (.S(S1), .D0(mux21_1_y), .D1(mux21_2_y), .Y(Y));
endmodule

module AOI22 (
  input  A,
  input  B,
  input  C,
  input  D,
  output Y
);

  wire transistor_1_out, transistor_4_out, transistor_8_out;

  Transistor transistor_1 (.in(1'b1), .out(transistor_1_out), .gate(C));
  Transistor transistor_2 (.in(transistor_1_out), .out(Y), .gate(A));
  Transistor #(.\type ("n")) transistor_3 (.in(transistor_4_out), .out(Y), .gate(A));
  Transistor #(.\type ("n")) transistor_4 (.in(1'b0), .out(transistor_4_out), .gate(B));
  Transistor transistor_5 (.in(1'b1), .out(transistor_1_out), .gate(D));
  Transistor transistor_6 (.in(transistor_1_out), .out(Y), .gate(B));
  Transistor #(.\type ("n")) transistor_7 (.in(transistor_8_out), .out(Y), .gate(C));
  Transistor #(.\type ("n")) transistor_8 (.in(1'b0), .out(transistor_8_out), .gate(D));
endmodule

module InvMux21 (
  input  S,
  input  D0,
  input  D1,
  output Ybar
);

  wire not_1_out;

  not not_1 (not_1_out, S);
  AOI22 aoi22_1 (.A(S), .B(D1), .C(not_1_out), .D(D0), .Y(Ybar));
endmodule

module AOI22Mux41 (
  input  S0,
  input  S1,
  input  D0,
  input  D1,
  input  D2,
  input  D3,
  output Y
);

  wire invmux21_1_ybar, invmux21_2_ybar;

  InvMux21 invmux21_1 (.S(S0), .D0(D0), .D1(D1), .Ybar(invmux21_1_ybar));
  InvMux21 invmux21_2 (.S(S0), .D0(D2), .D1(D3), .Ybar(invmux21_2_ybar));
  InvMux21 invmux21_3 (.S(S1), .D0(invmux21_1_ybar), .D1(invmux21_2_ybar), .Ybar(Y));
endmodule

module Mux81 (
  input  in_1,
  input  in_2,
  input  in_3,
  input  in_4,
  input  in_5,
  input  in_6,
  input  in_7,
  input  in_8,
  input  in_9,
  input  in_10,
  input  in_11,
  input  in_12,
  input  Y
);

  wire hierarchicalmux41_1_y, hierarchicalmux41_2_y;

  HierarchicalMux41 hierarchicalmux41_1 (
    .S0(in_9), .S1(in_11), .D0(in_1), .D1(in_2), .D2(in_3), .D3(in_5), .Y(hierarchicalmux41_1_y));
  HierarchicalMux41 hierarchicalmux41_2 (
    .S0(in_9), .S1(in_11), .D0(in_6), .D1(in_10), .D2(in_7), .D3(in_8), .Y(hierarchicalmux41_2_y));
  Mux21 mux21_1 (.S(in_12), .D0(hierarchicalmux41_1_y), .D1(hierarchicalmux41_2_y), .Y(Y));

  assign in_4 = in_3;

  // Other names for the same wires on the sheet: D0 = in_1; D1 = in_2; D2 = in_3; D3 = in_5; D4 = in_6; D5 = in_10;
  //   D6 = in_7; D7 = in_8; S0 = in_9; S1 = in_11; S2 = in_12
endmodule
