// Logisim project lab2_part1.circ as structural Verilog: 3 circuits, main circuit main
module main (
  input  In_0,
  input  In_1,
  input  In_2,
  input  In_3,
  input  Sel_0,
  input  Sel_1,
  output Out_1
);

  Mux_4to1 mux_4to1_1 (.In_0(In_0), .In_1(In_1), .In_2(In_2), .In_3(In_3), .Sel_0(Sel_0), .Sel_1(Sel_1), .out_7(Out_1));
endmodule

module Mux_2to1 (
  input  sel,
  input  in_0,
  input  in_1,
  output ou_1
);

  wire and_1_out, and_2_out, not_1_out;

  not not_1 (not_1_out, sel);
  and and_1 (and_1_out, sel, in_1);
  and and_2 (and_2_out, not_1_out, in_0);
  or or_1 (ou_1, and_2_out, and_1_out);
endmodule

module Mux_4to1 (
  input  In_0,
  input  In_1,
  input  In_2,
  input  In_3,
  input  Sel_0,
  input  Sel_1,
  output out_7
);

  wire mux_2to1_1_ou_1, mux_2to1_2_ou_1;

  Mux_2to1 mux_2to1_1 (.sel(Sel_0), .in_0(In_0), .in_1(In_1), .ou_1(mux_2to1_1_ou_1));
  Mux_2to1 mux_2to1_2 (.sel(Sel_0), .in_0(In_2), .in_1(In_3), .ou_1(mux_2to1_2_ou_1));
  Mux_2to1 mux_2to1_3 (.sel(Sel_1), .in_0(mux_2to1_1_ou_1), .in_1(mux_2to1_2_ou_1), .ou_1(out_7));
endmodule
