// Logisim project lab4_binary.circ as structural Verilog: 4 circuits, main circuit SequenceChecker
module SequenceChecker (
);

  wire clock_1_out, clock_2_out, comparator_1_eq, comparator_2_eq, keyboard_1_avail, or_1_out, R,
       sequencedetector_1_z, shift_register_1_p2, V;
  wire [3:0] undriven;
  wire [6:0] keyboard_1_data, subtractor_1_out;

  Clock clock_1 (.out(clock_1_out));
  Button Reset (.out(R));
  Clock clock_2 (.out(clock_2_out));
  Keyboard keyboard_1 (.clk(clock_2_out), .clr(R), .avail(keyboard_1_avail), .data(keyboard_1_data));  // open: re
  LED led_1 (.in(sequencedetector_1_z));
  SequenceDetector sequencedetector_1 (.W(V), .CLK(clock_1_out), .Reset(R), .Z(sequencedetector_1_z));
  // Shift_Register #(.length(4)) shift_register_1: pin names not known; wires that end beside it: R, shift_register_1_p2, V
  Clock clock_3 (.out(shift_register_1_p2));
  Subtractor #(.width(7)) subtractor_1 (
    .a(keyboard_1_data), .b(7'b0011110), .out(subtractor_1_out));  // open: bin, bout
  and and_1 (V, subtractor_1_out[0], keyboard_1_avail);
  Comparator #(.mode("unsigned"), .width(4)) comparator_1 (
    .a(undriven), .b(4'b1111), .eq(comparator_1_eq));  // open: gt, lt
  or or_1 (or_1_out, comparator_1_eq, comparator_2_eq);
  Comparator #(.mode("unsigned"), .width(4)) comparator_2 (
    .a(undriven), .b(4'b1101), .eq(comparator_2_eq));  // open: gt, lt
  LED led_2 (.in(or_1_out));

  // Notes on the sheet:
  //   1. Poke the reset button.
  //   2. Type only 1s and 0s into the keyboard by poking it.
  //   3. Toggle the clock and watch the keyboard sequence transfer to your FSM.
endmodule

module SequenceDetector (
  input  W,
  input  CLK,
  input  Reset,
  output Z
);

  wire [2:0] nextstatelogic_1_snext, StateRegister_q;

  NextStateLogic nextstatelogic_1 (.S(StateRegister_q), .W(W), .Snext(nextstatelogic_1_snext));
  Register #(.width(3)) StateRegister (
    .D(nextstatelogic_1_snext), .clk(CLK), .Q(StateRegister_q), .clr(Reset));  // open: en
  OutputLogic outputlogic_1 (.S(StateRegister_q), .Z(Z));
endmodule

module NextStateLogic (
  input  [2:0] S,
  input  W,
  output [2:0] Snext
);

  wire and_1_out, and_2_out, and_3_out, and_4_out, and_5_out, and_6_out, and_7_out, and_8_out, and_9_out,
       and_10_out, not_1_out, not_2_out, not_3_out, not_4_out;

  not not_1 (not_1_out, S[2]);
  not not_2 (not_2_out, S[1]);
  not not_3 (not_3_out, S[0]);
  not not_4 (not_4_out, W);
  and and_1 (and_1_out, not_1_out, S[1], not_4_out);
  and and_2 (and_2_out, S[1], S[0]);
  and and_3 (and_3_out, S[2], not_2_out, W);
  and and_4 (and_4_out, S[2], S[0]);
  and and_5 (and_5_out, not_1_out, not_2_out, S[0], W);
  and and_6 (and_6_out, S[1], not_3_out, W);
  and and_7 (and_7_out, S[2], not_3_out, W);
  and and_8 (and_8_out, not_1_out, not_3_out, W);
  and and_9 (and_9_out, S[2], S[0], W);
  and and_10 (and_10_out, not_1_out, S[1], W);
  or or_1 (Snext[2], and_1_out, and_2_out, and_3_out, and_4_out);
  or or_2 (Snext[1], and_5_out, and_6_out, and_7_out);
  or or_3 (Snext[0], and_8_out, and_9_out, and_10_out);
endmodule

module OutputLogic (
  input  [2:0] S,
  output Z
);

  wire and_1_out, and_2_out, not_1_out;

  not not_1 (not_1_out, S[1]);
  and and_1 (and_1_out, S[1], S[0]);
  and and_2 (and_2_out, S[2], not_1_out);
  or or_1 (Z, and_1_out, and_2_out);
endmodule
