// Logisim project lab4_demo.circ as structural Verilog: 6 circuits, main circuit GreatestCommonDivisor
module GreatestCommonDivisor (
  input  [7:0] A,
  input  [7:0] B,
  input  Ready
);

  wire clock_1_out, clock_2_out, controlunit_1_srca, controlunit_1_srcb, controlunit_1_wra,
       controlunit_1_wrb, Reset;
  wire [1:0] controlunit_1_op, sign;
  wire [7:0] datapath_1_result;

  Clock clock_1 (.out(clock_1_out));
  Button u_Reset (.out(Reset));
  ControlUnit controlunit_1 (
    .ready(Ready), .sign(sign), .CLK(clock_1_out), .Reset(Reset), .Op(controlunit_1_op),
    .SrcA(controlunit_1_srca), .SrcB(controlunit_1_srcb), .WrA(controlunit_1_wra), .WrB(controlunit_1_wrb));
  Clock clock_2 (.out(clock_2_out));
  Hex_Digit_Display #(.decimalPoint("false")) hex_digit_display_1 (.value(datapath_1_result[7:4]));
  Datapath datapath_1 (
    .A(A), .B(B), .Op(controlunit_1_op), .SrcA(controlunit_1_srca), .SrcB(controlunit_1_srcb),
    .WrA(controlunit_1_wra), .WrB(controlunit_1_wrb), .CLK(clock_2_out), .Reset(Reset),
    .Result(datapath_1_result), .Sign(sign));
  Hex_Digit_Display #(.decimalPoint("false")) hex_digit_display_2 (.value(datapath_1_result[3:0]));
endmodule

module Datapath (
  input  [7:0] A,
  input  [7:0] B,
  input  [1:0] Op,
  input  SrcA,
  input  SrcB,
  input  WrA,
  input  WrB,
  input  CLK,
  input  Reset,
  output [7:0] Result,
  output [1:0] Sign
);

  wire [7:0] multiplexer_1_out, multiplexer_2_out, RegA_q, RegB_q;

  Multiplexer #(.enable("true"), .width(8)) multiplexer_1 (
    .in0(Result), .in1(A), .out(multiplexer_1_out), .sel(SrcA));  // open: en
  Multiplexer #(.enable("true"), .width(8)) multiplexer_2 (
    .in0(Result), .in1(B), .out(multiplexer_2_out), .sel(SrcB));  // open: en
  Register RegA (.D(multiplexer_1_out), .en(WrA), .clk(CLK), .Q(RegA_q), .clr(Reset));
  Register RegB (.D(multiplexer_2_out), .en(WrB), .clk(CLK), .Q(RegB_q), .clr(Reset));
  ArithmeticUnit arithmeticunit_1 (.A(RegA_q), .B(RegB_q), .Op(Op), .Result(Result), .Sign(Sign));

  // Other names for the same wires on the sheet: Y[7:0] = Result
endmodule

module ArithmeticUnit (
  input  [7:0] A,
  input  [7:0] B,
  input  [1:0] Op,
  output [7:0] Result,
  output [1:0] Sign
);

  wire [7:0] multiplexer_1_out, multiplexer_2_out, subtractor_1_out;

  Multiplexer #(.width(8)) multiplexer_1 (.in0(A), .in1(B), .out(multiplexer_1_out));  // open: sel
  Multiplexer #(.width(8)) multiplexer_2 (.in0(B), .in1(A), .out(multiplexer_2_out), .sel(Op[0]));
  Subtractor subtractor_1 (.a(multiplexer_1_out), .b(multiplexer_2_out), .out(subtractor_1_out));  // open: bin, bout
  Multiplexer #(.width(8)) multiplexer_3 (.in0(multiplexer_1_out), .in1(subtractor_1_out), .out(Result));  // open: sel
  Comparator comparator_1 (.a(subtractor_1_out), .b({8{1'b0}}), .gt(Sign[0]), .lt(Sign[1]));  // open: eq
endmodule

module ControlUnit (
  input  ready,
  input  [1:0] sign,
  input  CLK,
  input  Reset,
  output [1:0] Op,
  output SrcA,
  output SrcB,
  output WrA,
  output WrB
);

  wire [2:0] nextstatelogic_1_snext, StateRegister_q;

  NextStateLogic nextstatelogic_1 (.S(StateRegister_q), .Ready(ready), .Sign(sign), .Snext(nextstatelogic_1_snext));
  Register #(.width(3)) StateRegister (
    .D(nextstatelogic_1_snext), .clk(CLK), .Q(StateRegister_q), .clr(Reset));  // open: en
  OutputLogic outputlogic_1 (.S(StateRegister_q), .Op(Op), .SrcA(SrcA), .SrcB(SrcB), .WrA(WrA), .WrB(WrB));
endmodule

module NextStateLogic (
  input  [2:0] S,
  input  Ready,
  input  [1:0] Sign,
  output [2:0] Snext
);
endmodule

module OutputLogic (
  input  [2:0] S,
  output [1:0] Op,
  output SrcA,
  output SrcB,
  output WrA,
  output WrB
);
endmodule
