// Logisim project lab4_one_hot.circ as structural Verilog: 5 circuits, main circuit SequenceChecker
module SequenceChecker (
);

  wire clock_1_out, clock_2_out, comparator_1_eq, comparator_2_eq, keyboard_1_avail, or_1_out, R,
       sequencedetector_1_z, shift_register_1_p2, V;
  wire [3:0] undriven;
  wire [6:0] keyboard_1_data, subtractor_1_out;

  Clock clock_1 (.out(clock_1_out));
  Button Reset (.out(R));
  Clock clock_2 (.out(clock_2_out));
  Keyboard keyboard_1 (.clk(clock_2_out), .clr(R), .avail(keyboard_1_avail), .data(keyboard_1_data));  // open: re
  LED led_1 (.in(sequencedetector_1_z));
  SequenceDetector sequencedetector_1 (.W(V), .CLK(clock_1_out), .Reset(R), .Z(sequencedetector_1_z));
  // Shift_Register #(.length(4)) shift_register_1: pin names not known; wires that end beside it: R, shift_register_1_p2, V
  Clock clock_3 (.out(shift_register_1_p2));
  Subtractor #(.width(7)) subtractor_1 (
    .a(keyboard_1_data), .b(7'b0011110), .out(subtractor_1_out));  // open: bin, bout
  and and_1 (V, subtractor_1_out[0], keyboard_1_avail);
  Comparator #(.mode("unsigned"), .width(4)) comparator_1 (
    .a(undriven), .b(4'b1111), .eq(comparator_1_eq));  // open: gt, lt
  or or_1 (or_1_out, comparator_1_eq, comparator_2_eq);
  Comparator #(.mode("unsigned"), .width(4)) comparator_2 (
    .a(undriven), .b(4'b1101), .eq(comparator_2_eq));  // open: gt, lt
  LED led_2 (.in(or_1_out));

  // Notes on the sheet:
  //   1. Poke the reset button.
  //   2. Type only 1s and 0s into the keyboard by poking it.
  //   3. Toggle the clock and watch the keyboard sequence transfer to your FSM.
endmodule

module SequenceDetector (
  input  W,
  input  CLK,
  input  Reset,
  output Z
);

  wire [6:0] nextstatelogic_1_snext, stateregister_1_q;

  NextStateLogic nextstatelogic_1 (.S(stateregister_1_q), .W(W), .Snext(nextstatelogic_1_snext));
  StateRegister stateregister_1 (.D(nextstatelogic_1_snext), .CLK(CLK), .Reset(Reset), .Q(stateregister_1_q));
  OutputLogic outputlogic_1 (.S(stateregister_1_q), .Z(Z));
endmodule

module NextStateLogic (
  input  [6:0] S,
  input  W,
  output [6:0] Snext
);
endmodule

module OutputLogic (
  input  [6:0] S,
  output Z
);
endmodule

module StateRegister (
  input  [6:0] D,
  input  CLK,
  input  Reset,
  output [6:0] Q
);

  D_Flip_Flop d_ff_1 (.D(D[0]), .clk(CLK), .Q(Q[0]), .reset(Reset));  // open: Qn, preset
  D_Flip_Flop d_ff_2 (.D(D[1]), .Q(Q[1]), .reset(Reset));  // open: clk, Qn, preset
  D_Flip_Flop d_ff_3 (.D(D[2]), .clk(CLK), .Q(Q[2]), .reset(Reset));  // open: Qn, preset
  D_Flip_Flop d_ff_4 (.D(D[3]), .clk(CLK), .Q(Q[3]), .reset(Reset));  // open: Qn, preset
  D_Flip_Flop d_ff_5 (.D(D[4]), .clk(CLK), .Q(Q[4]), .reset(Reset));  // open: Qn, preset
  D_Flip_Flop d_ff_6 (.D(D[5]), .clk(CLK), .Q(Q[5]), .reset(Reset));  // open: Qn, preset
  D_Flip_Flop d_ff_7 (.D(D[6]), .clk(CLK), .Q(Q[6]), .reset(Reset));  // open: Qn, preset
endmodule
