// Logisim project lab5_clock.circ as structural Verilog: 2 circuits, main circuit RateDividerChecker
module RateDivider (
  input  Reset,
  input  Enable,
  input  CLK,
  input  [1:0] Rate,
  output DivOut
);

  Counter counter_1 (.clr(Reset));  // open: load, up, count, clk, D, carry, Q
endmodule

module RateDividerChecker (
  input  Enable
);

  wire CLK, NewEnable, Reset;
  wire [1:0] Rate;
  wire [3:0] counter_1_q, counter_2_q;

  Button u_Reset (.out(Reset));
  Counter #(.max('hf), .width(4)) counter_1 (
    .count(NewEnable), .Q(counter_1_q), .clk(CLK), .clr(Reset));  // open: load, D, carry, up
  Clock clock_1 (.out(CLK));
  Hex_Digit_Display #(.decimalPoint("false")) hex_digit_display_1 (.value(counter_1_q));
  RateDivider ratedivider_1 (.Reset(Reset), .Enable(Enable), .CLK(CLK), .Rate(Rate), .DivOut(NewEnable));
  Hex_Digit_Display #(.decimalPoint("false")) hex_digit_display_2 (.value(counter_2_q));
  Counter #(.max('hf), .width(4)) counter_2 (
    .count(Enable), .Q(counter_2_q), .clk(CLK), .clr(Reset));  // open: load, D, carry, up
  Slider #(.width(2)) slider_1 (.out(Rate));

  // Other names for the same wires on the sheet: EN = Enable
endmodule
