// Logisim project lab5_counter.circ as structural Verilog: 5 circuits, main circuit CounterChecker
module CounterChecker (
  input  CountEnable
);

  wire CLK, CLR, comparator_1_eq, comparator_1_gt, comparator_1_lt, not_1_out, or_1_out;
  wire [7:0] LogiQ, MyQ;

  Clock clock_1 (.out(CLK));
  Hex_Digit_Display #(.decimalPoint("false")) hex_digit_display_1 (.value(MyQ[7:4]));
  Comparator comparator_1 (.a(MyQ), .b(LogiQ), .gt(comparator_1_gt), .eq(comparator_1_eq), .lt(comparator_1_lt));
  Hex_Digit_Display #(.decimalPoint("false")) hex_digit_display_2 (.value(MyQ[3:0]));
  LED led_1 (.in(comparator_1_eq));
  or or_1 (or_1_out, comparator_1_gt, comparator_1_lt);
  LED led_2 (.in(or_1_out));
  Hex_Digit_Display #(.decimalPoint("false")) hex_digit_display_3 (.value(LogiQ[7:4]));
  counter8 counter8_1 (.CountEnable(CountEnable), .CLK(CLK), .CLR(CLR), .Q(MyQ));
  Hex_Digit_Display #(.decimalPoint("false")) hex_digit_display_4 (.value(LogiQ[3:0]));
  Button Reset (.out(CLR));
  Counter #(.ongoal("continue")) counter_1 (
    .clr(CLR), .load(not_1_out), .up(1'b1), .clk(CLK), .Q(LogiQ));  // open: count, D, carry
  not not_1 (not_1_out, CountEnable);

  // Other names for the same wires on the sheet: EN = CountEnable

  // Notes on the sheet:
  //   1. Press the Reset button.
  //   2. Toggle CountEnable so that it is TRUE
  //   3. Go to "Simulate -> Auto-Tick Enabled" and watch the LEDs and Hex displays.
endmodule

module incrementer4 (
  input  CountEnable,
  input  Clock,
  input  Clear,
  output [3:0] Q
);

  wire and_1_out, and_2_out, and_3_out;

  T_Flip_Flop TFF0 (.T(CountEnable), .clk(Clock), .Q(Q[0]), .reset(Clear));  // open: Qn, preset
  and and_1 (and_1_out, CountEnable, Q[0]);
  T_Flip_Flop TFF1 (.T(and_1_out), .clk(Clock), .Q(Q[1]), .reset(Clear));  // open: Qn, preset
  and and_2 (and_2_out, and_1_out, Q[1]);
  T_Flip_Flop TFF2 (.T(and_2_out), .clk(Clock), .Q(Q[2]), .reset(Clear));  // open: Qn, preset
  and and_3 (and_3_out, and_2_out, Q[2]);
  T_Flip_Flop TFF3 (.T(and_3_out), .clk(Clock), .Q(Q[3]), .reset(Clear));  // open: Qn, preset
endmodule

module counter2 (
  input  CountEnable,
  input  CLK,
  input  CLR,
  output [1:0] Q
);

  T_Flip_Flop TFF0 (.T(CountEnable), .clk(CLK), .Q(Q[0]), .reset(CLR));  // open: Qn, preset
  T_Flip_Flop TFF1 (.T(Q[0]), .clk(CLK), .Q(Q[1]), .reset(CLR));  // open: Qn, preset

  // Other names for the same wires on the sheet: CE = CountEnable
endmodule

module counter4 (
  input  CountEnable,
  input  CLK,
  input  CLR,
  output [3:0] Q
);

  wire and_1_out;

  counter2 counter2_1 (.CountEnable(CountEnable), .CLK(CLK), .CLR(CLR), .Q(Q[1:0]));
  and and_1 (and_1_out, CountEnable, Q[0], Q[1]);
  counter2 counter2_2 (.CountEnable(and_1_out), .CLK(CLK), .CLR(CLR), .Q(Q[3:2]));

  // Other names for the same wires on the sheet: CE = CountEnable
endmodule

module counter8 (
  input  CountEnable,
  input  CLK,
  input  CLR,
  output [7:0] Q
);

  counter4 counter4_1 ();  // open: CountEnable, CLK, CLR, Q
  counter4 counter4_2 ();  // open: CountEnable, CLK, CLR, Q

  // Other names for the same wires on the sheet: CE = CountEnable
endmodule
